# Fritzing sketch Germinator_v1 (saved by Fritzing 0.9.2b)
circuit board: 22.5563cm x 10.6846cm
breadboards: 1

parts:
  LCD1 = LCD screen
  R1 = Rotary Potentiometer (Small) [maximum_resistance=100kΩ package=THT]
  DHT1 = DHT11 Humitidy and Temperature Sensor
  Composant1 = Arduino Uno (Rev3)
  PART1 = SparkFun Soil Moisture Sensor [part_number=SEN-13322]  # not connected

nets (from the pcb view):
  GND: LCD1.VSS, LCD1.LED+, LCD1.LED-, R1.leg2, DHT1.GND, Composant1.GND
  VDD: LCD1.VDD, R1.leg1, DHT1.VDD, Composant1.5V
  N1: LCD1.V0, R1.wiper
  N2: LCD1.RS, Composant1.D9_PWM
  N3: LCD1.E, Composant1.D8
  N4: LCD1.DB4, Composant1.D10_PWM/SS
  N5: LCD1.DB5, Composant1.D11_PWM/MOSI
  N6: LCD1.DB6, Composant1.D12/MISO
  N7: LCD1.DB7, Composant1.D13/SCK
  N8: DHT1.DATA, Composant1.D3_PWM

custom parts:
  DHT11 Humitidy and Temperature Sensor: DHT11 Humidity and Temperature Sensor
  SparkFun Soil Moisture Sensor: The SparkFun Soil Moisture Sensor is a simple breakout for measuring the moisture in soil and similar materials.
